# Fritzing sketch ir-cut-off (saved by Fritzing 0.9.3b)
breadboards: 1

parts:
  Raspberry_Pi_1 = Raspberry Pi 3 [part_number=RPI-3-V1.2]
  IC1 = L293D [package=THT]
  M1 = DC Motor

nets:
  N1: Raspberry_Pi_1.GIPO25, IC1.In_1
  N2: Raspberry_Pi_1.GND, IC1.0V
  N3: Raspberry_Pi_1.GIPO24, IC1.In_2
  N4: Raspberry_Pi_1.GIPO23, IC1.Enable_1
  N5: Raspberry_Pi_1.5V, IC1.+Vmotor, IC1.+V
  N6: IC1.Out_1_(_Controlled_by_Enable_1_), M1.pin_2
  N7: IC1.Out_2_(_Controlled_by_Enable_1_), M1.pin_1

// code stored in the sketch: ir-cutoff.ino

