# Fritzing sketch main-schema (saved by Fritzing 0.9.3b)

parts:
  Raspberry_Pi_3B+ = Raspberry Pi 3 [part_number=RPI-3-V1.2]
  U2 = RELAY [package=relay-jzc]
  D1 = Diode [package=diode-1n4148]
  Q1 = NPN-Transistor [package="TO92 [THT]"]
  R1 = Resistor [tolerance=±5% resistance=1k package="2010 [SMD]"]
  R2 = PHOTOCELL [package=photocell-kit]
  S1 = Pushbutton [package="[SMD]"]
  V1 = AC Power [voltage=5 frequency=60]
  L1 = Solenoid
  U3 = Transformer [package=transformer]

nets:
  N1: Raspberry_Pi_3B+.GND, Q1.E, R2.P$2, S1.Pin_1
  N2: Raspberry_Pi_3B+.GIPO19, R1.Pin_0
  N3: Raspberry_Pi_3B+.GIPO21, S1.Pin_3, S1.Pin_4
  N4: Raspberry_Pi_3B+.GIPO20, R2.P$1
  N5: Raspberry_Pi_3B+.5V, U2.COIL1, D1.C
  N6: U2.COIL2, D1.A, Q1.C
  N7: U2.NC, U3.1
  N8: U2.NO, L1.pin2
  N9: Q1.B, R1.Pin_1
  N10: V1.V+, U3.4
  N11: V1.V-, U3.3
  N12: L1.pin1, U3.2
